// Logisim project Aluproject.circ as structural Verilog: 19 circuits, main circuit sub4bit
module halfsub (
  input  a,
  input  b,
  output d,
  output out_4
);

  wire n7408_1_pin2, n7486_1_pin6;

  _7486 u_7486_1 (
    .pin1(a), .pin2(b), .pin3(d), .pin6(n7486_1_pin6), .pin9(n7486_1_pin6));  // open: pin4, pin5, pin13, pin12, pin11, pin10, pin8
  _7408 u_7408_1 (
    .pin1(b), .pin2(n7408_1_pin2), .pin3(out_4));  // open: pin4, pin5, pin6, pin13, pin12, pin11, pin10, pin9, pin8
  not not_1 (n7408_1_pin2, a);

  // Notes on the sheet:
  //   7408 and
  //   7486 xor
  //   7400 nand
  //   7402 nor
  //   7432 or
endmodule

module fullsubraction (
  input  A,
  input  B,
  input  Bin,
  output D,
  output Bout
);

  wire halfsub_1_d, halfsub_1_out_4, halfsub_2_out_4;

  halfsub halfsub_1 (.a(A), .b(B), .d(halfsub_1_d), .out_4(halfsub_1_out_4));
  halfsub halfsub_2 (.a(halfsub_1_d), .b(Bin), .d(D), .out_4(halfsub_2_out_4));
  _7432 u_7432_1 (
    .pin1(halfsub_2_out_4), .pin2(halfsub_1_out_4), .pin3(Bout));  // open: pin4, pin5, pin6, pin13, pin12, pin11, pin10, pin9, pin8

  // Notes on the sheet:
  //   7432 or
endmodule

module sub4bit (
  input  [3:0] A,
  input  [3:0] B,
  input  BorrowIn,
  output [3:0] D,
  output borrow
);

  wire fullsubraction_1_bout, fullsubraction_2_bout, fullsubraction_3_bout;

  fullsubraction fullsubraction_1 (.A(A[0]), .B(B[0]), .Bin(BorrowIn), .D(D[0]), .Bout(fullsubraction_1_bout));
  fullsubraction fullsubraction_2 (
    .A(A[1]), .B(B[1]), .Bin(fullsubraction_1_bout), .D(D[1]), .Bout(fullsubraction_2_bout));
  fullsubraction fullsubraction_3 (
    .A(A[2]), .B(B[2]), .Bin(fullsubraction_2_bout), .D(D[2]), .Bout(fullsubraction_3_bout));
  fullsubraction fullsubraction_4 (.A(A[3]), .B(B[3]), .Bin(fullsubraction_3_bout), .D(D[3]), .Bout(borrow));
endmodule

module OpCode (
  input  A0,
  input  A1,
  input  A2,
  output [7:0] Opcod
);

  wire n7408_1_pin3, n7408_1_pin6, n7408_1_pin8, n7408_1_pin11, not_1_out, not_2_out, not_3_out;

  not not_1 (not_1_out, A0);
  not not_2 (not_2_out, A1);
  not not_3 (not_3_out, A2);
  _7408 u_7408_1 (
    .pin1(A2), .pin2(A1), .pin3(n7408_1_pin3), .pin4(not_3_out), .pin5(A1), .pin6(n7408_1_pin6), .pin13(A2),
    .pin12(not_2_out), .pin11(n7408_1_pin11), .pin10(not_3_out), .pin9(not_2_out), .pin8(n7408_1_pin8));
  _7408 u_7408_2 (
    .pin1(not_1_out), .pin2(n7408_1_pin8), .pin3(Opcod[0]), .pin4(n7408_1_pin8), .pin5(A0), .pin6(Opcod[1]),
    .pin13(n7408_1_pin6), .pin12(not_1_out), .pin11(Opcod[2]), .pin10(n7408_1_pin6), .pin9(A0),
    .pin8(Opcod[3]));
  _7408 u_7408_3 (
    .pin1(n7408_1_pin11), .pin2(not_1_out), .pin3(Opcod[4]), .pin4(n7408_1_pin11), .pin5(A0),
    .pin6(Opcod[5]), .pin13(n7408_1_pin3), .pin12(not_1_out), .pin11(Opcod[6]), .pin10(n7408_1_pin3),
    .pin9(A0), .pin8(Opcod[7]));

  // Notes on the sheet:
  //   7408 and
  //   7400 nand
  //   7402 nor
  //   7432 or
  //   7486 xor
  //   notc
  //   notb
  //   nota
  //   and3
  //   000 add
  //   001 sub
  //   010 mult
  //   100 and
  //   101 or
  //   110 
  //   add toplama
  //   sub çıkarma
  //   mult çarpma
  //   and aynı ise o sayıyı verir farklıysa sıfır verir
  //   xor aynıysa sıfır verir farklıysa binary işlem yapar
endmodule

module \logic  (
  input  [2:0] Opcod,
  input  [3:0] A,
  input  [3:0] B,
  output [3:0] resultA,
  output [3:0] result0,
  output [3:0] resultX
);

  wire n7408_1_pin3, n7408_1_pin6, n7408_1_pin8, n7408_1_pin11, n7432_1_pin3, n7432_1_pin6, n7432_1_pin8,
       n7432_1_pin11, n7486_1_pin3, n7486_1_pin6, n7486_1_pin8, n7486_1_pin11;

  _7408 u_7408_1 (
    .pin1(A[0]), .pin2(B[0]), .pin3(n7408_1_pin3), .pin4(B[1]), .pin5(A[1]), .pin6(n7408_1_pin6),
    .pin13(A[2]), .pin12(B[2]), .pin11(n7408_1_pin11), .pin10(A[3]), .pin9(B[3]), .pin8(n7408_1_pin8));
  _7432 u_7432_1 (
    .pin1(A[0]), .pin2(B[0]), .pin3(n7432_1_pin3), .pin4(A[1]), .pin5(B[1]), .pin6(n7432_1_pin6),
    .pin13(A[2]), .pin12(B[2]), .pin11(n7432_1_pin11), .pin10(A[3]), .pin9(B[3]), .pin8(n7432_1_pin8));
  _7486 u_7486_1 (
    .pin1(A[0]), .pin2(B[0]), .pin3(n7486_1_pin3), .pin4(A[1]), .pin5(B[1]), .pin6(n7486_1_pin6),
    .pin13(A[2]), .pin12(B[2]), .pin11(n7486_1_pin11), .pin10(A[3]), .pin9(B[3]), .pin8(n7486_1_pin8));
  _7408 u_7408_2 (
    .pin1(Opcod[0]), .pin2(n7408_1_pin3), .pin3(resultA[0]), .pin4(Opcod[0]), .pin5(n7408_1_pin6),
    .pin6(resultA[1]), .pin13(Opcod[0]), .pin12(n7408_1_pin11), .pin11(resultA[2]), .pin10(Opcod[0]),
    .pin9(n7408_1_pin8), .pin8(resultA[3]));
  _7408 u_7408_3 (
    .pin1(Opcod[1]), .pin2(n7432_1_pin3), .pin3(result0[0]), .pin4(Opcod[1]), .pin5(n7432_1_pin6),
    .pin6(result0[1]), .pin13(Opcod[1]), .pin12(n7432_1_pin11), .pin11(result0[2]), .pin10(Opcod[1]),
    .pin9(n7432_1_pin8), .pin8(result0[3]));
  _7408 u_7408_4 (
    .pin1(Opcod[2]), .pin2(n7486_1_pin3), .pin3(resultX[0]), .pin4(Opcod[2]), .pin5(n7486_1_pin6),
    .pin6(resultX[1]), .pin13(Opcod[2]), .pin12(n7486_1_pin11), .pin11(resultX[2]), .pin10(Opcod[2]),
    .pin9(n7486_1_pin8), .pin8(resultX[3]));

  // Notes on the sheet:
  //   001 and
  //   010 or
  //   100 xor
  //   7408 and
  //   7432 or
  //   7486 xor
  //   7402 nor
  //   7400 nand
  //   and12
  //   and10
  //   and13
  //   and11
  //   or12
  //   or10
  //   or13
  //   or11
  //   xor10
  //   xor12
  //   xor11
  //   xor13
  //   resultA0
  //   resultA1
  //   result02
  //   result00
  //   result03
  //   resul01
  //   resultX0
  //   resultX3
  //   resultX2
  //   resultX1
  //   resultA
  //   result0
  //   resultX
endmodule

module addition (
  input  cin,
  input  [3:0] A,
  input  [3:0] B,
  output [3:0] Y,
  output CarryOut,
  output overflow
);

  wire fulladder_1_carryo, fulladder_2_carryo, fulladder_3_carryo;

  fulladder fulladder_1 (.Cin(A[0]), .A(B[0]), .B(cin), .Sum(Y[0]), .CarryO(fulladder_1_carryo));
  fulladder fulladder_2 (.Cin(A[1]), .A(B[1]), .B(fulladder_1_carryo), .Sum(Y[1]), .CarryO(fulladder_2_carryo));
  fulladder fulladder_3 (.Cin(A[2]), .A(B[2]), .B(fulladder_2_carryo), .Sum(Y[2]), .CarryO(fulladder_3_carryo));
  fulladder fulladder_4 (.Cin(A[3]), .A(B[3]), .B(fulladder_3_carryo), .Sum(Y[3]), .CarryO(CarryOut));
  xor xor_1 (overflow, CarryOut, fulladder_3_carryo);
endmodule

module fulladder (
  input  Cin,
  input  A,
  input  B,
  output Sum,
  output CarryO
);

  wire n7408_1_pin8, n7408_1_pin10, n7408_1_pin11;

  _7408 u_7408_1 (
    .pin13(A), .pin12(B), .pin11(n7408_1_pin11), .pin10(n7408_1_pin10), .pin9(Cin), .pin8(n7408_1_pin8));  // open: pin1, pin2, pin3, pin4, pin5, pin6
  // _7432 7432_1: pin names not known; wires that end beside it: 1'b1, n7408_1_pin11, n7408_1_pin8, CarryO, 1'b0
  _7486 u_7486_1 (
    .pin13(B), .pin12(A), .pin11(n7408_1_pin10), .pin10(n7408_1_pin10), .pin9(Cin), .pin8(Sum));  // open: pin1, pin2, pin3, pin4, pin5, pin6

  // Notes on the sheet:
  //   7408 and
  //   7432 or
  //   7486 xor
endmodule

module halfadd (
  input  A,
  input  B,
  output sum,
  output carry
);

  _7486 u_7486_1 (.pin1(A), .pin2(B), .pin3(sum));  // open: pin4, pin5, pin6, pin13, pin12, pin11, pin10, pin9, pin8
  _7408 u_7408_1 (.pin1(A), .pin2(B), .pin3(carry));  // open: pin4, pin5, pin6, pin13, pin12, pin11, pin10, pin9, pin8

  // Notes on the sheet:
  //   7408 and
  //   7486 xor
  //   7432 or
endmodule

module arithmeticUnit (
  input  [1:0] Opcod,
  input  CarryIn,
  input  [3:0] A,
  input  [3:0] B,
  output [3:0] add_Y,
  output [3:0] Sub_Y,
  output CarryOUT,
  output overflow
);

  wire n7408_1_pin2, n7408_1_pin8, n7408_1_pin9, n7408_1_pin11, n7408_1_pin13;
  wire [3:0] addition_1_y, sub4bit_1_d;

  _7408 u_7408_1 (
    .pin1(Opcod[0]), .pin2(n7408_1_pin2), .pin3(overflow), .pin13(n7408_1_pin13), .pin12(Opcod[0]),
    .pin11(n7408_1_pin11), .pin10(Opcod[1]), .pin9(n7408_1_pin9), .pin8(n7408_1_pin8));  // open: pin4, pin5, pin6
  addition addition_1 (
    .cin(CarryIn), .A(A), .B(B), .Y(addition_1_y), .CarryOut(n7408_1_pin13), .overflow(n7408_1_pin2));
  sub4bit sub4bit_1 (.A(A), .B(B), .BorrowIn(CarryIn), .D(sub4bit_1_d), .borrow(n7408_1_pin9));
  // _7432 7432_1: pin names not known; wires that end beside it: 1'b1, n7408_1_pin11, n7408_1_pin8, CarryOUT, 1'b0
  _7408 u_7408_2 (
    .pin1(addition_1_y[2]), .pin2(Opcod[0]), .pin3(add_Y[2]), .pin4(Opcod[0]), .pin5(addition_1_y[3]),
    .pin6(add_Y[3]), .pin13(addition_1_y[0]), .pin12(Opcod[0]), .pin11(add_Y[0]), .pin10(addition_1_y[1]),
    .pin9(Opcod[0]), .pin8(add_Y[1]));
  _7408 u_7408_3 (
    .pin1(sub4bit_1_d[2]), .pin2(Opcod[1]), .pin3(Sub_Y[2]), .pin4(Opcod[1]), .pin5(sub4bit_1_d[3]),
    .pin6(Sub_Y[3]), .pin13(sub4bit_1_d[0]), .pin12(Opcod[1]), .pin11(Sub_Y[0]), .pin10(Opcod[1]),
    .pin9(sub4bit_1_d[1]), .pin8(Sub_Y[1]));

  // Notes on the sheet:
  //   opCoded CarryO
  //   switch 2 add 01
  //   switch 1 sub 10
  //   decoded opcode
  //   add_Y0
  //   addy_2
  //   sub_y0
  //   sub_y2
  //   add_y1
  //   add_y3
  //   sub_y1
  //   sub_y3
  //   7432 or
  //   7486 xor
  //   7402 nor
  //   7408 and
  //   7400 nand
endmodule

module aritmatiktest (
  input  in_1
);

  wire arithmeticunit_1_carryout, arithmeticunit_1_overflow, bcd_to_7_segment_decoder_3_p1,
       bcd_to_7_segment_decoder_6_p1, bcd_to_7_segment_decoder_9_p1, bcd_to_7_segment_decoder_12_p1,
       binary_to_bcd_converter_1_p2, binary_to_bcd_converter_1_p4, binary_to_bcd_converter_2_p2,
       binary_to_bcd_converter_2_p4, binary_to_bcd_converter_3_p2, binary_to_bcd_converter_3_p4,
       binary_to_bcd_converter_4_p3, binary_to_bcd_converter_4_p5;
  wire [1:0] dipswitch_1_sw2;
  wire [3:0] arithmeticunit_1_add_y, arithmeticunit_1_sub_y, dipswitch_2_p1, dipswitch_2_p5;

  DipSwitch #(.number(2)) dipswitch_1 (.sw1(dipswitch_1_sw2[1]), .sw2(dipswitch_1_sw2[0]));
  // DipSwitch dipswitch_2: pin names not known; wires that end beside it: dipswitch_2_p1[0], dipswitch_2_p1[1], dipswitch_2_p1[2], dipswitch_2_p1[3], dipswitch_2_p5[0], dipswitch_2_p5[1], dipswitch_2_p5[2], dipswitch_2_p5[3]
  _7_Segment_Display u_7_segment_display_1 ();  // open: g, f, a, b, e, d, c, dp
  // BCD_to_7_Segment_decoder bcd_to_7_segment_decoder_1: pin names not known
  // Binary_to_BCD_converter binary_to_bcd_converter_1: pin names not known; wires that end beside it: {{5{1'b0}}, dipswitch_2_p1}, binary_to_bcd_converter_1_p2, binary_to_bcd_converter_1_p2, binary_to_bcd_converter_1_p4
  _7_Segment_Display u_7_segment_display_2 ();  // open: g, f, a, b, e, d, c, dp
  // BCD_to_7_Segment_decoder bcd_to_7_segment_decoder_2: pin names not known; wires that end beside it: binary_to_bcd_converter_1_p4
  _7_Segment_Display u_7_segment_display_3 ();  // open: g, f, a, b, e, d, c, dp
  // BCD_to_7_Segment_decoder bcd_to_7_segment_decoder_3: pin names not known; wires that end beside it: bcd_to_7_segment_decoder_3_p1, bcd_to_7_segment_decoder_3_p1
  arithmeticUnit arithmeticunit_1 (
    .Opcod(dipswitch_1_sw2), .CarryIn(in_1), .A(dipswitch_2_p1), .B(dipswitch_2_p5),
    .add_Y(arithmeticunit_1_add_y), .Sub_Y(arithmeticunit_1_sub_y), .CarryOUT(arithmeticunit_1_carryout),
    .overflow(arithmeticunit_1_overflow));
  LED led_1 (.in(arithmeticunit_1_overflow));
  _7_Segment_Display u_7_segment_display_4 ();  // open: g, f, a, b, e, d, c, dp
  // BCD_to_7_Segment_decoder bcd_to_7_segment_decoder_4: pin names not known
  // Binary_to_BCD_converter binary_to_bcd_converter_2: pin names not known; wires that end beside it: {{5{1'b0}}, dipswitch_2_p5}, binary_to_bcd_converter_2_p2, binary_to_bcd_converter_2_p2, binary_to_bcd_converter_2_p4
  LED led_2 (.in(arithmeticunit_1_carryout));
  _7_Segment_Display u_7_segment_display_5 ();  // open: g, f, a, b, e, d, c, dp
  _7_Segment_Display u_7_segment_display_6 ();  // open: g, f, a, b, e, d, c, dp
  // BCD_to_7_Segment_decoder bcd_to_7_segment_decoder_5: pin names not known; wires that end beside it: binary_to_bcd_converter_2_p4
  // BCD_to_7_Segment_decoder bcd_to_7_segment_decoder_6: pin names not known; wires that end beside it: bcd_to_7_segment_decoder_6_p1, bcd_to_7_segment_decoder_6_p1
  _7_Segment_Display u_7_segment_display_7 ();  // open: g, f, a, b, e, d, c, dp
  // BCD_to_7_Segment_decoder bcd_to_7_segment_decoder_7: pin names not known
  // Binary_to_BCD_converter binary_to_bcd_converter_3: pin names not known; wires that end beside it: {{5{1'b0}}, arithmeticunit_1_add_y}, binary_to_bcd_converter_3_p2, binary_to_bcd_converter_3_p2, binary_to_bcd_converter_3_p4
  _7_Segment_Display u_7_segment_display_8 ();  // open: g, f, a, b, e, d, c, dp
  // BCD_to_7_Segment_decoder bcd_to_7_segment_decoder_8: pin names not known; wires that end beside it: binary_to_bcd_converter_3_p4
  _7_Segment_Display u_7_segment_display_9 ();  // open: g, f, a, b, e, d, c, dp
  // BCD_to_7_Segment_decoder bcd_to_7_segment_decoder_9: pin names not known; wires that end beside it: bcd_to_7_segment_decoder_9_p1, bcd_to_7_segment_decoder_9_p1
  _7_Segment_Display u_7_segment_display_10 ();  // open: g, f, a, b, e, d, c, dp
  // BCD_to_7_Segment_decoder bcd_to_7_segment_decoder_10: pin names not known
  // Binary_to_BCD_converter binary_to_bcd_converter_4: pin names not known; wires that end beside it: 1'b0, {{5{1'b0}}, arithmeticunit_1_sub_y}, binary_to_bcd_converter_4_p3, binary_to_bcd_converter_4_p3, binary_to_bcd_converter_4_p5
  _7_Segment_Display u_7_segment_display_11 ();  // open: g, f, a, b, e, d, c, dp
  // BCD_to_7_Segment_decoder bcd_to_7_segment_decoder_11: pin names not known; wires that end beside it: binary_to_bcd_converter_4_p5
  _7_Segment_Display u_7_segment_display_12 ();  // open: g, f, a, b, e, d, c, dp
  // BCD_to_7_Segment_decoder bcd_to_7_segment_decoder_12: pin names not known; wires that end beside it: bcd_to_7_segment_decoder_12_p1, bcd_to_7_segment_decoder_12_p1

  // Notes on the sheet:
  //   switch 2 add 01
  //   switch 1 sub 10
  //   decoded opcode
  //   A
  //   B
  //   A
  //   A
  //   elde var 1 durumunda
  //   B
  //   browout-Bit taşımmında yanar
endmodule

module bit4multiplier (
  input  [3:0] A,
  input  [3:0] B,
  output [7:0] Y
);

  wire [2:0] n7408_1_pin8;
  wire [3:0] addition4_1_carryo, n7408_2_pin11, n7408_3_pin11, n7408_4_pin11;
  wire [3:1] addition4_2_sum;
  wire [3:3] addition4_2_carryo;

  _7408 u_7408_1 (
    .pin1(B[0]), .pin2(A[2]), .pin3(n7408_1_pin8[1]), .pin4(B[0]), .pin5(A[3]), .pin6(n7408_1_pin8[2]),
    .pin13(B[0]), .pin12(A[0]), .pin11(Y[0]), .pin10(B[0]), .pin9(A[1]), .pin8(n7408_1_pin8[0]));
  _7408 u_7408_2 (
    .pin1(A[2]), .pin2(B[2]), .pin3(n7408_2_pin11[2]), .pin4(B[2]), .pin5(A[3]), .pin6(n7408_2_pin11[3]),
    .pin13(A[0]), .pin12(B[2]), .pin11(n7408_2_pin11[0]), .pin10(A[1]), .pin9(B[2]), .pin8(n7408_2_pin11[1]));
  _7408 u_7408_3 (
    .pin1(B[3]), .pin2(A[2]), .pin3(n7408_3_pin11[2]), .pin4(A[3]), .pin5(B[3]), .pin6(n7408_3_pin11[3]),
    .pin13(A[0]), .pin12(B[3]), .pin11(n7408_3_pin11[0]), .pin10(A[1]), .pin9(B[3]), .pin8(n7408_3_pin11[1]));
  _7408 u_7408_4 (
    .pin1(A[2]), .pin2(B[1]), .pin3(n7408_4_pin11[2]), .pin4(A[3]), .pin5(B[1]), .pin6(n7408_4_pin11[3]),
    .pin13(A[0]), .pin12(B[1]), .pin11(n7408_4_pin11[0]), .pin10(A[1]), .pin9(B[1]), .pin8(n7408_4_pin11[1]));
  addition4 addition4_1 (
    .CarryIn(1'b0), .A(n7408_4_pin11), .B({1'b0, n7408_1_pin8}), .Sum({addition4_1_carryo[2:0], Y[1]}),
    .CarryO(addition4_1_carryo[3]));
  addition4 addition4_2 (
    .CarryIn(1'b0), .A(n7408_2_pin11), .B(addition4_1_carryo), .Sum({addition4_2_sum, Y[2]}),
    .CarryO(addition4_2_carryo[3]));
  addition4 addition4_3 (
    .CarryIn(1'b0), .A(n7408_3_pin11), .B({addition4_2_carryo[3], addition4_2_sum}), .Sum(Y[6:3]),
    .CarryO(Y[7]));

  // Notes on the sheet:
  //   7408 and
  //   7432 or
  //   7486 xor
  //   7402 nor
  //   7400 nand
endmodule

module fulladd (
  input  A,
  input  B,
  input  Carry,
  output sum,
  output Cout
);

  wire and_1_out, and_2_out, xor_1_out;

  xor xor_1 (xor_1_out, A, B);
  xor xor_2 (sum, xor_1_out, Carry);
  and and_1 (and_1_out, xor_1_out, Carry);
  and and_2 (and_2_out, B, A);
  or or_1 (Cout, and_1_out, and_2_out);
endmodule

module addition4 (
  input  CarryIn,
  input  [3:0] A,
  input  [3:0] B,
  output [3:0] Sum,
  output CarryO
);

  wire fulladder_1_carryo, fulladder_2_carryo, fulladder_3_carryo;

  fulladder fulladder_1 (.Cin(CarryIn), .A(A[0]), .B(B[0]), .Sum(Sum[0]), .CarryO(fulladder_1_carryo));
  fulladder fulladder_2 (.Cin(fulladder_1_carryo), .A(A[1]), .B(B[1]), .Sum(Sum[1]), .CarryO(fulladder_2_carryo));
  fulladder fulladder_3 (.Cin(fulladder_2_carryo), .A(A[2]), .B(B[2]), .Sum(Sum[2]), .CarryO(fulladder_3_carryo));
  fulladder fulladder_4 (.Cin(fulladder_3_carryo), .A(A[3]), .B(B[3]), .Sum(Sum[3]), .CarryO(CarryO));

  // Notes on the sheet:
  //   7408 and
  //   7432 or
  //   7486 xor
  //   7402 nor
  //   7400 nand
endmodule

module alu (
  input  [2:0] opC,
  input  Cin,
  input  [3:0] A,
  input  [3:0] B,
  output overflow,
  output Cout,
  output [7:0] Y
);

  wire n7408_1_pin3, n7408_1_pin6, n7408_1_pin8, n7408_1_pin11, n7408_3_pin3, n7408_3_pin6, n7408_3_pin8,
       n7408_3_pin11, n7408_4_pin3, n7408_4_pin6, n7408_4_pin8, n7408_4_pin11, n7432_1_pin2, n7432_1_pin3,
       n7432_1_pin5, n7432_1_pin6, n7432_1_pin8, n7432_1_pin10, n7432_1_pin11, n7432_1_pin12, n7432_3_pin3,
       n7432_3_pin6, n7432_3_pin8, n7432_3_pin11, n7432_4_pin3, n7432_4_pin6, n7432_4_pin8, n7432_4_pin11;
  wire [1:0] opcode_1_opcod;
  wire [2:0] opcode_1_opcod_2;
  wire [3:0] arithmeticunit_1_add_y, arithmeticunit_1_sub_y, logic_1_result0, logic_1_resulta,
       logic_1_resultx;
  wire [7:0] n7408_1_pin12;
  wire [7:2] n7408_1_pin1;

  _7408 u_7408_1 (
    .pin1(n7408_1_pin1[2]), .pin2(n7408_1_pin12[2]), .pin3(n7408_1_pin3), .pin4(n7408_1_pin12[3]),
    .pin5(n7408_1_pin1[2]), .pin6(n7408_1_pin6), .pin13(n7408_1_pin1[2]), .pin12(n7408_1_pin12[0]),
    .pin11(n7408_1_pin11), .pin10(n7408_1_pin1[2]), .pin9(n7408_1_pin12[1]), .pin8(n7408_1_pin8));
  _7408 u_7408_2 (
    .pin1(n7408_1_pin1[2]), .pin2(n7408_1_pin12[6]), .pin3(Y[6]), .pin4(n7408_1_pin12[7]),
    .pin5(n7408_1_pin1[2]), .pin6(Y[7]), .pin13(n7408_1_pin1[2]), .pin12(n7408_1_pin12[4]), .pin11(Y[4]),
    .pin10(n7408_1_pin1[2]), .pin9(n7408_1_pin12[5]), .pin8(Y[5]));
  bit4multiplier bit4multiplier_1 (.A(A), .B(B), .Y(n7408_1_pin12));
  OpCode opcode_1 (
    .A0(opC[0]), .A1(opC[1]), .A2(opC[2]),
    .Opcod({n7408_1_pin1[7], opcode_1_opcod_2, n7408_1_pin1[3:2], opcode_1_opcod}));
  arithmeticUnit arithmeticunit_1 (
    .Opcod(opcode_1_opcod), .CarryIn(Cin), .A(A), .B(B), .add_Y(arithmeticunit_1_add_y),
    .Sub_Y(arithmeticunit_1_sub_y), .CarryOUT(overflow), .overflow(Cout));
  \logic  logic_1 (
    .Opcod(opcode_1_opcod_2), .A(A), .B(B), .resultA(logic_1_resulta), .result0(logic_1_result0),
    .resultX(logic_1_resultx));
  _7408 u_7408_3 (
    .pin1(arithmeticunit_1_add_y[2]), .pin2(opcode_1_opcod[0]), .pin3(n7408_3_pin3),
    .pin4(arithmeticunit_1_add_y[3]), .pin5(opcode_1_opcod[0]), .pin6(n7408_3_pin6),
    .pin13(arithmeticunit_1_add_y[0]), .pin12(opcode_1_opcod[0]), .pin11(n7408_3_pin11),
    .pin10(arithmeticunit_1_add_y[1]), .pin9(opcode_1_opcod[0]), .pin8(n7408_3_pin8));
  _7408 u_7408_4 (
    .pin1(arithmeticunit_1_sub_y[2]), .pin2(opcode_1_opcod[1]), .pin3(n7408_4_pin3),
    .pin4(arithmeticunit_1_sub_y[3]), .pin5(opcode_1_opcod[1]), .pin6(n7408_4_pin6),
    .pin13(arithmeticunit_1_sub_y[0]), .pin12(opcode_1_opcod[1]), .pin11(n7408_4_pin11),
    .pin10(arithmeticunit_1_sub_y[1]), .pin9(opcode_1_opcod[1]), .pin8(n7408_4_pin8));
  _7432 u_7432_1 (
    .pin1(logic_1_resultx[2]), .pin2(n7432_1_pin2), .pin3(n7432_1_pin3), .pin4(logic_1_resultx[3]),
    .pin5(n7432_1_pin5), .pin6(n7432_1_pin6), .pin13(logic_1_resultx[1]), .pin12(n7432_1_pin12),
    .pin11(n7432_1_pin11), .pin10(n7432_1_pin10), .pin9(logic_1_resultx[0]), .pin8(n7432_1_pin8));
  _7432 u_7432_2 (
    .pin1(logic_1_resulta[2]), .pin2(logic_1_result0[2]), .pin3(n7432_1_pin2), .pin4(logic_1_result0[3]),
    .pin5(logic_1_resulta[3]), .pin6(n7432_1_pin5), .pin13(logic_1_result0[1]), .pin12(logic_1_resulta[1]),
    .pin11(n7432_1_pin12), .pin10(logic_1_result0[0]), .pin9(logic_1_resulta[0]), .pin8(n7432_1_pin10));
  _7432 u_7432_3 (
    .pin1(n7408_3_pin3), .pin2(n7408_4_pin3), .pin3(n7432_3_pin3), .pin4(n7408_4_pin6), .pin5(n7408_3_pin6),
    .pin6(n7432_3_pin6), .pin13(n7408_3_pin11), .pin12(n7408_4_pin11), .pin11(n7432_3_pin11),
    .pin10(n7408_3_pin8), .pin9(n7408_4_pin8), .pin8(n7432_3_pin8));
  _7432 u_7432_4 (
    .pin1(n7432_3_pin3), .pin2(n7432_1_pin3), .pin3(n7432_4_pin3), .pin4(n7432_3_pin6), .pin5(n7432_1_pin6),
    .pin6(n7432_4_pin6), .pin13(n7432_3_pin11), .pin12(n7432_1_pin8), .pin11(n7432_4_pin11),
    .pin10(n7432_3_pin8), .pin9(n7432_1_pin11), .pin8(n7432_4_pin8));
  _7432 u_7432_5 (
    .pin1(n7432_4_pin8), .pin2(n7408_1_pin8), .pin3(Y[1]), .pin4(n7408_1_pin11), .pin5(n7432_4_pin11),
    .pin6(Y[0]), .pin13(n7432_4_pin3), .pin12(n7408_1_pin3), .pin11(Y[2]), .pin10(n7432_4_pin6),
    .pin9(n7408_1_pin6), .pin8(Y[3]));

  // Notes on the sheet:
  //   6
  //   0
  //   1
  //   4
  //   5
  //   7
  //   3
  //   2
  //   1
  //   000 add
  //   001 sub
  //   010 mult
  //   100 and
  //   101 or
  //   110 xor
  //   2
  //   2
  //   1
  //   0
  //   temp0
  //   temp1
  //   temp3
  //   0
  //   1
  //   3
  //   2
  //   add toplama
  //   sub çıkarma
  //   mult çarpma
  //   add
  //   1
  //   sub
  //   3
  //   and aynı ise o sayıyı verir farklıysa sıfır verir
  //   2
  //   0
  //   xor aynıysa sıfır verir farklıysa binary işlem yapar
  //   3
  //   2
  //   3
  //   0
  //   1
  //   3
  //   2
  //   0
  //   1
  //   2
  //   3
  //   7408 and
  //   7432 or
  //   7486 xor
  //   7402 nor
  //   7400 nand
  //   0
  //   2
  //   1
  //   3
endmodule

module Alutest (
  input  in_1
);

  wire alu_1_cout, alu_1_overflow, bcd_to_7_segment_decoder_3_p1, bcd_to_7_segment_decoder_5_p1,
       bcd_to_7_segment_decoder_8_p1, bcd_to_7_segment_decoder_9_p1, binary_to_bcd_converter_1_p2,
       binary_to_bcd_converter_1_p4, binary_to_bcd_converter_2_p2, binary_to_bcd_converter_2_p4,
       binary_to_bcd_converter_3_p2;
  wire [2:0] dipswitch_1_sw3;
  wire [3:0] dipswitch_2_p1, dipswitch_2_p5;
  wire [7:0] alu_1_y;

  DipSwitch #(.number(3)) dipswitch_1 (.sw1(dipswitch_1_sw3[2]), .sw2(dipswitch_1_sw3[1]), .sw3(dipswitch_1_sw3[0]));
  // DipSwitch dipswitch_2: pin names not known; wires that end beside it: dipswitch_2_p1[0], dipswitch_2_p1[1], dipswitch_2_p1[2], dipswitch_2_p1[3], dipswitch_2_p5[0], dipswitch_2_p5[1], dipswitch_2_p5[2], dipswitch_2_p5[3]
  _7_Segment_Display u_7_segment_display_1 ();  // open: g, f, a, b, e, d, c, dp
  // BCD_to_7_Segment_decoder bcd_to_7_segment_decoder_1: pin names not known
  // Binary_to_BCD_converter binary_to_bcd_converter_1: pin names not known; wires that end beside it: {{5{1'b0}}, dipswitch_2_p1}, binary_to_bcd_converter_1_p2, binary_to_bcd_converter_1_p2, binary_to_bcd_converter_1_p4
  _7_Segment_Display u_7_segment_display_2 ();  // open: g, f, a, b, e, d, c, dp
  // BCD_to_7_Segment_decoder bcd_to_7_segment_decoder_2: pin names not known; wires that end beside it: binary_to_bcd_converter_1_p4
  _7_Segment_Display u_7_segment_display_3 ();  // open: g, f, a, b, e, d, c, dp
  // BCD_to_7_Segment_decoder bcd_to_7_segment_decoder_3: pin names not known; wires that end beside it: bcd_to_7_segment_decoder_3_p1, bcd_to_7_segment_decoder_3_p1
  LED led_1 (.in(alu_1_overflow));
  alu alu_1 (
    .opC(dipswitch_1_sw3), .Cin(in_1), .A(dipswitch_2_p1), .B(dipswitch_2_p5), .overflow(alu_1_overflow),
    .Cout(alu_1_cout), .Y(alu_1_y));
  _7_Segment_Display u_7_segment_display_4 ();  // open: g, f, a, b, e, d, c, dp
  // BCD_to_7_Segment_decoder bcd_to_7_segment_decoder_4: pin names not known
  // Binary_to_BCD_converter binary_to_bcd_converter_2: pin names not known; wires that end beside it: {{5{1'b0}}, dipswitch_2_p5}, binary_to_bcd_converter_2_p2, binary_to_bcd_converter_2_p2, binary_to_bcd_converter_2_p4
  LED led_2 (.in(alu_1_cout));
  _7_Segment_Display u_7_segment_display_5 ();  // open: g, f, a, b, e, d, c, dp
  _7_Segment_Display u_7_segment_display_6 ();  // open: g, f, a, b, e, d, c, dp
  // BCD_to_7_Segment_decoder bcd_to_7_segment_decoder_5: pin names not known; wires that end beside it: bcd_to_7_segment_decoder_5_p1
  // BCD_to_7_Segment_decoder bcd_to_7_segment_decoder_6: pin names not known; wires that end beside it: binary_to_bcd_converter_2_p4
  _7_Segment_Display u_7_segment_display_7 ();  // open: g, f, a, b, e, d, c, dp
  _7_Segment_Display u_7_segment_display_8 ();  // open: g, f, a, b, e, d, c, dp
  // BCD_to_7_Segment_decoder bcd_to_7_segment_decoder_7: pin names not known; wires that end beside it: bcd_to_7_segment_decoder_5_p1
  // BCD_to_7_Segment_decoder bcd_to_7_segment_decoder_8: pin names not known; wires that end beside it: bcd_to_7_segment_decoder_8_p1
  // Binary_to_BCD_converter binary_to_bcd_converter_3: pin names not known; wires that end beside it: {1'b0, alu_1_y}, binary_to_bcd_converter_3_p2, binary_to_bcd_converter_3_p2, bcd_to_7_segment_decoder_8_p1
  _7_Segment_Display u_7_segment_display_9 ();  // open: g, f, a, b, e, d, c, dp
  // BCD_to_7_Segment_decoder bcd_to_7_segment_decoder_9: pin names not known; wires that end beside it: bcd_to_7_segment_decoder_9_p1, bcd_to_7_segment_decoder_9_p1

  // Notes on the sheet:
  //   A
  //   B
  //   000 add
  //   001 sub
  //   010 mult
  //   100 and
  //   101 or
  //   110 xor 
  //   sub çıkarma
  //   mult çarpma
  //   add toplama en fazla 15 gösterir  
  //   A
  //    negatif sonuçta led yanar
  //   and aynı ise o sayıyı verir farklıysa sıfır verir
  //           aynıysa o sayıyı verir farklıysa toplar binary işlem yapar
  //   xor aynıysa sıfır verir farklıysa binary işlem yapar
  //   B
  //   15 den yüksek değerlerde led yanar
endmodule

module addtest (
);

  wire addition_1_carryout, addition_1_overflow, button_1_out, n7_segment_display_1_p1,
       n7_segment_display_2_p1;
  wire [3:0] addition_1_y, dipswitch_1_p4, dipswitch_1_p8;

  // DipSwitch dipswitch_1: pin names not known; wires that end beside it: dipswitch_1_p4[3], dipswitch_1_p4[2], dipswitch_1_p4[1], dipswitch_1_p4[0], dipswitch_1_p8[3], dipswitch_1_p8[2], dipswitch_1_p8[1], dipswitch_1_p8[0]
  Button button_1 (.out(button_1_out));
  addition addition_1 (
    .cin(button_1_out), .A(dipswitch_1_p4), .B(dipswitch_1_p8), .Y(addition_1_y),
    .CarryOut(addition_1_carryout), .overflow(addition_1_overflow));
  LED led_1 (.in(addition_1_overflow));
  LED led_2 (.in(addition_1_carryout));
  // _7_Segment_Display 7_segment_display_1: pin names not known; wires that end beside it: n7_segment_display_1_p1, n7_segment_display_1_p1
  // BCD_to_7_Segment_decoder bcd_to_7_segment_decoder_1: pin names not known
  // Binary_to_BCD_converter binary_to_bcd_converter_1: pin names not known
  // _7_Segment_Display 7_segment_display_2: pin names not known; wires that end beside it: n7_segment_display_2_p1, n7_segment_display_2_p1
  // BCD_to_7_Segment_decoder bcd_to_7_segment_decoder_2: pin names not known

  // Notes on the sheet:
  //   A
  //   B
  //   4 bitlik çıkış alır en büyük sayı 15
endmodule

module subtest (
);

  wire button_1_out, n7_segment_display_1_p1, n7_segment_display_2_p1, sub4bit_1_borrow;
  wire [3:0] dipswitch_1_p4, dipswitch_1_p8, sub4bit_1_d;

  Button button_1 (.out(button_1_out));
  // DipSwitch dipswitch_1: pin names not known; wires that end beside it: dipswitch_1_p4[3], dipswitch_1_p4[2], dipswitch_1_p4[1], dipswitch_1_p4[0], dipswitch_1_p8[3], dipswitch_1_p8[2], dipswitch_1_p8[1], dipswitch_1_p8[0]
  sub4bit sub4bit_1 (
    .A(dipswitch_1_p4), .B(dipswitch_1_p8), .BorrowIn(button_1_out), .D(sub4bit_1_d),
    .borrow(sub4bit_1_borrow));
  LED led_1 (.in(sub4bit_1_borrow));
  // Binary_to_BCD_converter binary_to_bcd_converter_1: pin names not known
  // _7_Segment_Display 7_segment_display_1: pin names not known; wires that end beside it: n7_segment_display_1_p1, n7_segment_display_1_p1
  // _7_Segment_Display 7_segment_display_2: pin names not known; wires that end beside it: n7_segment_display_2_p1, n7_segment_display_2_p1
  // BCD_to_7_Segment_decoder bcd_to_7_segment_decoder_1: pin names not known
  // BCD_to_7_Segment_decoder bcd_to_7_segment_decoder_2: pin names not known

  // Notes on the sheet:
  //   A-B
  //   A
  //   B
  //   negatif answer
endmodule

module logictest (
);

  wire bcd_to_7_segment_decoder_1_p1, bcd_to_7_segment_decoder_2_p2, bcd_to_7_segment_decoder_3_p1,
       bcd_to_7_segment_decoder_4_p1, bcd_to_7_segment_decoder_5_p1, bcd_to_7_segment_decoder_6_p1;
  wire [2:0] dipswitch_1_p3;
  wire [3:0] dipswitch_2_p1, dipswitch_2_p5, logic_1_result0, logic_1_resulta, logic_1_resultx;

  // DipSwitch #(.number(3)) dipswitch_1: pin names not known; wires that end beside it: dipswitch_1_p3[2], dipswitch_1_p3[1], dipswitch_1_p3[0]
  // DipSwitch dipswitch_2: pin names not known; wires that end beside it: dipswitch_2_p1[0], dipswitch_2_p1[1], dipswitch_2_p1[2], dipswitch_2_p1[3], dipswitch_2_p5[0], dipswitch_2_p5[1], dipswitch_2_p5[2], dipswitch_2_p5[3]
  \logic  logic_1 (
    .Opcod(dipswitch_1_p3), .A(dipswitch_2_p1), .B(dipswitch_2_p5), .resultA(logic_1_resulta),
    .result0(logic_1_result0), .resultX(logic_1_resultx));
  _7_Segment_Display u_7_segment_display_1 ();  // open: g, f, a, b, e, d, c, dp
  // BCD_to_7_Segment_decoder bcd_to_7_segment_decoder_1: pin names not known; wires that end beside it: bcd_to_7_segment_decoder_1_p1
  // Binary_to_BCD_converter binary_to_bcd_converter_1: pin names not known; wires that end beside it: bcd_to_7_segment_decoder_1_p1
  _7_Segment_Display u_7_segment_display_2 ();  // open: g, f, a, b, e, d, c, dp
  // BCD_to_7_Segment_decoder bcd_to_7_segment_decoder_2: pin names not known; wires that end beside it: 1'b0, bcd_to_7_segment_decoder_2_p2
  // Binary_to_BCD_converter binary_to_bcd_converter_2: pin names not known; wires that end beside it: 1'b0, 1'b0, bcd_to_7_segment_decoder_2_p2
  _7_Segment_Display u_7_segment_display_3 ();  // open: g, f, a, b, e, d, c, dp
  // BCD_to_7_Segment_decoder bcd_to_7_segment_decoder_3: pin names not known; wires that end beside it: bcd_to_7_segment_decoder_3_p1, bcd_to_7_segment_decoder_3_p1
  _7_Segment_Display u_7_segment_display_4 ();  // open: g, f, a, b, e, d, c, dp
  // BCD_to_7_Segment_decoder bcd_to_7_segment_decoder_4: pin names not known; wires that end beside it: bcd_to_7_segment_decoder_4_p1, bcd_to_7_segment_decoder_4_p1
  _7_Segment_Display u_7_segment_display_5 ();  // open: g, f, a, b, e, d, c, dp
  // BCD_to_7_Segment_decoder bcd_to_7_segment_decoder_5: pin names not known; wires that end beside it: bcd_to_7_segment_decoder_5_p1
  // Binary_to_BCD_converter binary_to_bcd_converter_3: pin names not known; wires that end beside it: bcd_to_7_segment_decoder_5_p1
  _7_Segment_Display u_7_segment_display_6 ();  // open: g, f, a, b, e, d, c, dp
  // BCD_to_7_Segment_decoder bcd_to_7_segment_decoder_6: pin names not known; wires that end beside it: bcd_to_7_segment_decoder_6_p1, bcd_to_7_segment_decoder_6_p1

  // Notes on the sheet:
  //   A
  //   B
  //   001 and
  //   010 or
  //   100 xor
  //   and
  //   or
  //   xor
endmodule

module multitest (
);

  wire n7_segment_display_1_p1, n7_segment_display_2_p1, n7_segment_display_3_p1;
  wire [3:0] dipswitch_1_p4, dipswitch_1_p8;
  wire [7:0] bit4multiplier_1_y;

  // DipSwitch dipswitch_1: pin names not known; wires that end beside it: dipswitch_1_p4[3], dipswitch_1_p4[2], dipswitch_1_p4[1], dipswitch_1_p4[0], dipswitch_1_p8[3], dipswitch_1_p8[2], dipswitch_1_p8[1], dipswitch_1_p8[0]
  bit4multiplier bit4multiplier_1 (.A(dipswitch_1_p4), .B(dipswitch_1_p8), .Y(bit4multiplier_1_y));
  // _7_Segment_Display 7_segment_display_1: pin names not known; wires that end beside it: n7_segment_display_1_p1, n7_segment_display_1_p1
  // BCD_to_7_Segment_decoder bcd_to_7_segment_decoder_1: pin names not known
  // _7_Segment_Display 7_segment_display_2: pin names not known; wires that end beside it: n7_segment_display_2_p1, n7_segment_display_2_p1
  // BCD_to_7_Segment_decoder bcd_to_7_segment_decoder_2: pin names not known
  // Binary_to_BCD_converter binary_to_bcd_converter_1: pin names not known
  // _7_Segment_Display 7_segment_display_3: pin names not known; wires that end beside it: n7_segment_display_3_p1, n7_segment_display_3_p1
  // BCD_to_7_Segment_decoder bcd_to_7_segment_decoder_3: pin names not known

  // Notes on the sheet:
  //   A
  //   B
endmodule
